// Logisim project projectCS125- jawza alanazi.circ as structural Verilog: 3 circuits, main circuit FA-1Bit
module FA_1Bit (
  input  A,
  input  B,
  input  Cin,
  output Sum,
  output Carry
);

  wire and_1_out, and_2_out, xor_1_out;

  xor xor_1 (xor_1_out, A, B);
  and and_1 (and_1_out, A, B);
  and and_2 (and_2_out, xor_1_out, Cin);
  xor xor_2 (Sum, xor_1_out, Cin);
  or or_1 (Carry, and_2_out, and_1_out);

  // Notes on the sheet:
  //   Jawza Fahad Alanazi - 443020299
  //   Task 1 : FA-1BIT
endmodule

module ALU_1Bit (
  input  Cin,
  input  Sub,
  input  A,
  input  B,
  input  [2:0] OPCODE,
  input  Shr_A,
  input  Shl_A,
  output R,
  output Cout
);

  wire and_1_out, fa_1bit_1_sum, or_1_out, xnor_1_out, xor_1_out, xor_2_out;

  xor xor_1 (xor_1_out, B, Sub);
  and and_1 (and_1_out, B, A);
  or or_1 (or_1_out, B, A);
  xor xor_2 (xor_2_out, B, A);
  xnor xnor_1 (xnor_1_out, B, A);
  FA_1Bit fa_1bit_1 (.A(A), .B(xor_1_out), .Cin(Cin), .Sum(fa_1bit_1_sum), .Carry(Cout));
  Multiplexer #(.select(3), .enable("false")) multiplexer_1 (
    .in0(and_1_out), .in1(or_1_out), .in2(xor_2_out), .in3(xnor_1_out), .in4(fa_1bit_1_sum), .in5(Shr_A),
    .in6(Shl_A), .out(R), .sel(OPCODE));  // open: in7

  // Notes on the sheet:
  //   Jawza Fahad Alnanazi - 443020299
  //   Task 2: ALU-1BIT
endmodule

module ALU (
  input  SUB,
  input  [2:0] OP,
  input  [7:0] A,
  input  Shift,
  input  [7:0] B,
  output [7:0] R,
  output Cout
);

  wire alu_1bit_1_cout, alu_1bit_2_cout, alu_1bit_3_cout, alu_1bit_4_cout, alu_1bit_5_cout, alu_1bit_6_cout,
       alu_1bit_7_cout;

  ALU_1Bit alu_1bit_1 (
    .R(R[0]), .Cout(alu_1bit_1_cout), .Cin(SUB), .Sub(SUB), .A(A[0]), .B(B[0]), .OPCODE(OP), .Shr_A(A[1]),
    .Shl_A(Shift));
  ALU_1Bit alu_1bit_2 (
    .R(R[1]), .Cout(alu_1bit_2_cout), .Cin(alu_1bit_1_cout), .Sub(SUB), .A(A[1]), .B(B[1]), .OPCODE(OP),
    .Shr_A(A[2]), .Shl_A(A[0]));
  ALU_1Bit alu_1bit_3 (
    .R(R[2]), .Cout(alu_1bit_3_cout), .Cin(alu_1bit_2_cout), .Sub(SUB), .A(A[2]), .B(B[2]), .OPCODE(OP),
    .Shr_A(A[3]), .Shl_A(A[1]));
  ALU_1Bit alu_1bit_4 (
    .R(R[3]), .Cout(alu_1bit_4_cout), .Cin(alu_1bit_3_cout), .Sub(SUB), .A(A[3]), .B(B[3]), .OPCODE(OP),
    .Shr_A(A[4]), .Shl_A(A[2]));
  ALU_1Bit alu_1bit_5 (
    .R(R[4]), .Cout(alu_1bit_5_cout), .Cin(alu_1bit_4_cout), .Sub(SUB), .A(A[4]), .B(B[4]), .OPCODE(OP),
    .Shr_A(A[5]), .Shl_A(A[3]));
  ALU_1Bit alu_1bit_6 (
    .R(R[5]), .Cout(alu_1bit_6_cout), .Cin(alu_1bit_5_cout), .Sub(SUB), .A(A[5]), .B(B[5]), .OPCODE(OP),
    .Shr_A(A[6]), .Shl_A(A[4]));
  ALU_1Bit alu_1bit_7 (
    .R(R[6]), .Cout(alu_1bit_7_cout), .Cin(alu_1bit_6_cout), .Sub(SUB), .A(A[6]), .B(B[6]), .OPCODE(OP),
    .Shr_A(A[7]), .Shl_A(A[5]));
  ALU_1Bit alu_1bit_8 (
    .R(R[7]), .Cout(Cout), .Cin(alu_1bit_7_cout), .Sub(SUB), .A(A[7]), .B(B[7]), .OPCODE(OP), .Shr_A(Shift),
    .Shl_A(A[6]));

  // Notes on the sheet:
  //   Jawza Fahad Alanazi - 443020299
  //   Task 3&4: ALU & shift 
endmodule
